# Fritzing sketch switch (saved by Fritzing 0.9.4)
breadboards: 2

parts:
  MCU1 = Raspberry Pi Zero
  S1 = Momentary Switch [package=ksa_sealed_tac_switch]
  LED1 = smd LED [color="Red (633nm)" package="1206 [SMD]"]
  R1 = Resistor [tolerance=±5% resistance=10k package="0402 [SMD]"]
  R2 = Resistor [tolerance=±5% resistance=1k package="0402 [SMD]"]

nets:
  N1: MCU1.pin_1, S1.4
  N2: MCU1.pin_9, MCU1.pin_30, MCU1.pin_34, LED1.cathode, R1.Pin_1
  N3: MCU1.pin_29, S1.2, R1.Pin_0
  N4: MCU1.pin_36, R2.Pin_1
  N5: LED1.anode, R2.Pin_0
